# Fritzing sketch Sketch (saved by Fritzing 0.9.3b)
breadboards: 1

parts:
  Raspberry_Pi_1 = Raspberry Pi 3 [part_number=RPI-3-V1.2]
  U1 = LCD-16X2 [package=lcd-16x2_noholes]
  S1 = Pushbutton [package="[THT]"]
  S2 = Pushbutton [package="[THT]"]
  S3 = Pushbutton [package="[THT]"]
  R1 = Resistor [tolerance=±5% resistance=220 package="0402 [SMD]"]

nets:
  N1: Raspberry_Pi_1.GIPO17, U1.DB6
  N2: Raspberry_Pi_1.GIPO5, U1.DB4
  N3: Raspberry_Pi_1.GIPO6, U1.DB5
  5V: Raspberry_Pi_1.GIPO19, Raspberry_Pi_1.GIPO20, Raspberry_Pi_1.GIPO16, Raspberry_Pi_1.5V, U1.VDD, U1.A, S1.Pin_3, S1.Pin_4, S2.Pin_3, S2.Pin_4, S3.Pin_3, S3.Pin_4
  N4: Raspberry_Pi_1.GIPO21, U1.E
  N5: Raspberry_Pi_1.GIPO12, U1.RS
  N6: Raspberry_Pi_1.GIPO18, U1.DB7
  GND: Raspberry_Pi_1.GND, U1.VSS, U1.R_W, U1.K, R1.Pin_1
  N7: U1.VO, R1.Pin_0
  N8: S1.Pin_1, S1.Pin_2
  N9: S2.Pin_1, S2.Pin_2
  N10: S3.Pin_1, S3.Pin_2
